// Logisim project Lab_3  reimaginged.circ as structural Verilog: 2 circuits, main circuit main
module main (
);

  wire button_1_out, toggle_1_out_2;

  Button button_1 (.out(button_1_out));
  Toggle toggle_1 (.in_1(button_1_out), .out_2(toggle_1_out_2));
  LED led_1 (.in(toggle_1_out_2));
endmodule

module Toggle (
  input  in_1,
  output out_2
);

  wire and_1_out, and_2_out, and_3_out, and_4_out, and_5_out, clock_1_out, d_ff_1_q, d_ff_2_q, not_1_out,
       not_2_out, not_3_out, not_4_out, not_5_out, or_1_out;

  Clock clock_1 (.out(clock_1_out));
  not not_1 (not_1_out, in_1);
  not not_2 (not_2_out, d_ff_1_q);
  not not_3 (not_3_out, d_ff_2_q);
  not not_4 (not_4_out, d_ff_2_q);
  not not_5 (not_5_out, d_ff_1_q);
  and and_1 (and_1_out, not_2_out, d_ff_2_q, not_1_out);
  and and_2 (and_2_out, d_ff_1_q, not_3_out);
  and and_3 (and_3_out, in_1, d_ff_1_q);
  and and_4 (and_4_out, not_5_out, d_ff_2_q);
  or or_1 (or_1_out, and_1_out, and_2_out, and_3_out);
  and and_5 (and_5_out, not_4_out, d_ff_1_q);
  D_Flip_Flop d_ff_1 (.clk(clock_1_out), .D(or_1_out), .Q(d_ff_1_q));  // open: Qn, preset, en, reset
  D_Flip_Flop d_ff_2 (.clk(clock_1_out), .D(in_1), .Q(d_ff_2_q));  // open: Qn, preset, en, reset
  or or_2 (out_2, and_5_out, and_4_out);
endmodule
