// Logisim project lab3_3.circ as structural Verilog: 3 circuits, main circuit main
module main (
  input  in_1
);

  wire A_C_out, and_1_out, and_2_out, and_3_out, and_4_out, and_5_out, and_6_out, and_7_out, clock_1_out,
       D0_out, D1_out, D2_out, D3_out, Engine_out, flip_flop_1_out_2, flip_flop_2_out_2, flip_flop_3_out_2,
       flip_flop_4_out_2, flip_flop_5_out_2, flip_flop_6_out_2, flip_flop_7_out_2, not_1_out, not_2_out,
       not_3_out, not_4_out, not_5_out, not_6_out, not_7_out, not_8_out, not_9_out, not_10_out, not_11_out,
       not_12_out, not_13_out, not_14_out, not_15_out, not_16_out, not_17_out, not_18_out, or_1_out,
       or_2_out, or_3_out, or_4_out, t_ff_1_q, t_ff_2_q, t_ff_3_q, t_ff_4_q, t_ff_5_q, t_ff_6_q, t_ff_7_q,
       Wipers_out;

  Clock clock_1 (.out(clock_1_out));
  Button D0 (.out(D0_out));
  Button D1 (.out(D1_out));
  Button D2 (.out(D2_out));
  Button D3 (.out(D3_out));
  Button A_C (.out(A_C_out));
  Button Engine (.out(Engine_out));
  Button Wipers (.out(Wipers_out));
  or or_1 (or_1_out, D0_out, A_C_out);
  or or_2 (or_2_out, D1_out, A_C_out, Engine_out);
  or or_3 (or_3_out, D2_out, Engine_out, Wipers_out);
  or or_4 (or_4_out, D3_out, Wipers_out);
  not not_1 (not_1_out, or_2_out);
  not not_2 (not_2_out, or_3_out);
  not not_3 (not_3_out, or_4_out);
  not not_4 (not_4_out, or_1_out);
  not not_5 (not_5_out, or_3_out);
  not not_6 (not_6_out, or_4_out);
  not not_7 (not_7_out, or_1_out);
  not not_8 (not_8_out, or_2_out);
  not not_9 (not_9_out, or_4_out);
  and and_1 (and_1_out, or_1_out, not_1_out, in_1, not_2_out, not_3_out);
  and and_2 (and_2_out, not_4_out, or_2_out, in_1, not_5_out, not_6_out);
  and and_3 (and_3_out, not_7_out, not_8_out, in_1, or_3_out, not_9_out);
  not not_10 (not_10_out, or_1_out);
  not not_11 (not_11_out, or_2_out);
  and and_4 (and_4_out, not_10_out, not_11_out, in_1, not_12_out, or_4_out);
  not not_12 (not_12_out, or_3_out);
  and and_5 (and_5_out, or_1_out, or_2_out, in_1, not_13_out, not_14_out);
  not not_13 (not_13_out, or_3_out);
  not not_14 (not_14_out, or_4_out);
  not not_15 (not_15_out, or_1_out);
  and and_6 (and_6_out, not_15_out, or_2_out, in_1, or_3_out, not_16_out);
  not not_16 (not_16_out, or_4_out);
  not not_17 (not_17_out, or_1_out);
  not not_18 (not_18_out, or_2_out);
  and and_7 (and_7_out, not_17_out, not_18_out, in_1, or_3_out, or_4_out);
  T_Flip_Flop t_ff_1 (.clk(clock_1_out), .T(and_1_out), .Q(t_ff_1_q));  // open: Qn, preset, reset, en
  T_Flip_Flop t_ff_2 (.clk(clock_1_out), .T(and_2_out), .Q(t_ff_2_q));  // open: Qn, preset, reset, en
  T_Flip_Flop t_ff_3 (.clk(clock_1_out), .T(and_3_out), .Q(t_ff_3_q));  // open: Qn, preset, reset, en
  T_Flip_Flop t_ff_4 (.clk(clock_1_out), .T(and_4_out), .Q(t_ff_4_q));  // open: Qn, preset, reset, en
  T_Flip_Flop t_ff_5 (.clk(clock_1_out), .T(and_5_out), .Q(t_ff_5_q));  // open: Qn, preset, reset, en
  T_Flip_Flop t_ff_6 (.clk(clock_1_out), .T(and_6_out), .Q(t_ff_6_q));  // open: Qn, preset, reset, en
  T_Flip_Flop t_ff_7 (.clk(clock_1_out), .T(and_7_out), .Q(t_ff_7_q));  // open: Qn, preset, reset, en
  flip_flop flip_flop_1 (.in_1(t_ff_1_q), .out_2(flip_flop_1_out_2));
  flip_flop flip_flop_2 (.in_1(t_ff_2_q), .out_2(flip_flop_2_out_2));
  flip_flop flip_flop_3 (.in_1(t_ff_3_q), .out_2(flip_flop_3_out_2));
  flip_flop flip_flop_4 (.in_1(t_ff_4_q), .out_2(flip_flop_4_out_2));
  flip_flop flip_flop_5 (.in_1(t_ff_5_q), .out_2(flip_flop_5_out_2));
  flip_flop flip_flop_6 (.in_1(t_ff_6_q), .out_2(flip_flop_6_out_2));
  flip_flop flip_flop_7 (.in_1(t_ff_7_q), .out_2(flip_flop_7_out_2));
  LED led_1 (.in(flip_flop_1_out_2));
  LED led_2 (.in(flip_flop_2_out_2));
  LED led_3 (.in(flip_flop_3_out_2));
  LED led_4 (.in(flip_flop_4_out_2));
  LED led_5 (.in(flip_flop_5_out_2));
  LED led_6 (.in(flip_flop_6_out_2));
  LED led_7 (.in(flip_flop_7_out_2));
endmodule

module toggle (
  output out_1
);

  wire and_1_out, and_2_out, and_3_out, and_4_out, and_5_out, and_6_out, and_7_out, and_8_out, button_1_out,
       clock_1_out, nor_1_out, nor_4_out, not_1_out, not_2_out, not_3_out, undriven, xor_1_out;

  Button button_1 (.out(button_1_out));
  Clock clock_1 (.out(clock_1_out));
  not not_1 (not_1_out, xor_1_out);
  xor xor_1 (xor_1_out, button_1_out, undriven);
  and and_1 (and_1_out, xor_1_out, clock_1_out);
  and and_2 (and_2_out, not_1_out, clock_1_out);
  and and_3 (and_3_out, and_1_out, clock_1_out);
  and and_4 (and_4_out, and_2_out, clock_1_out);
  not not_2 (not_2_out, clock_1_out);
  not nor_1 (nor_1_out, and_3_out);  // NOR_Gate
  // NOR_Gate nor_2 has open pins: in0=nor_1_out, in1=and_4_out, out=open
  not not_3 (not_3_out, nor_1_out);
  and and_5 (and_5_out, nor_1_out, not_2_out);
  and and_6 (and_6_out, not_3_out, not_2_out);
  and and_7 (and_7_out, and_5_out, not_2_out);
  and and_8 (and_8_out, not_2_out, and_6_out);
  nor nor_3 (out_1, and_7_out, nor_4_out);
  nor nor_4 (nor_4_out, undriven, and_8_out);
endmodule

module flip_flop (
  input  in_1,
  output out_2
);

  wire and_1_out, and_2_out, and_3_out, and_4_out, clock_1_out, nor_1_out, nor_2_out, nor_4_out, not_1_out,
       not_2_out, not_3_out;

  not not_1 (not_1_out, in_1);
  Clock clock_1 (.out(clock_1_out));
  and and_1 (and_1_out, clock_1_out, in_1);
  and and_2 (and_2_out, not_1_out, clock_1_out);
  not not_2 (not_2_out, clock_1_out);
  nor nor_1 (nor_1_out, and_1_out, nor_2_out);
  nor nor_2 (nor_2_out, nor_1_out, and_2_out);
  not not_3 (not_3_out, nor_1_out);
  and and_3 (and_3_out, nor_1_out, not_2_out);
  and and_4 (and_4_out, not_2_out, not_3_out);
  nor nor_3 (out_2, and_3_out, nor_4_out);
  not nor_4 (nor_4_out, and_4_out);  // NOR_Gate
endmodule
