// Logisim project PC.circ as structural Verilog: 7 circuits, main circuit main
module main (
  input  [3:0] RB,
  output [3:0] icode,
  output [3:0] ifun,
  output [3:0] RA,
  output [15:0] Val_P,
  output [31:0] Val_C
);

  wire [15:0] undriven;

  Fetch fetch_1 (
    .PC_IN(undriven), .Icode(icode), .ifun(ifun), .RA(RA), .RB(RB), .Val_C(Val_C));  // open: Halt, enable, PC_out
  PC pc_1 (.Input(undriven), .Output(Val_P));  // open: input_enabler, Clear
  PC_INCREMENT pc_increment_1 (.PC_IN(undriven), .PC_OUTPUT(Val_P));
  New_PC new_pc_1 (.icode(icode), .val_c(Val_C), .out_4(Val_P));  // open: Val_p
endmodule

module New_PC (
  input  [3:0] icode,
  input  [31:0] val_c,
  input  [15:0] Val_p,
  output [15:0] out_4
);


  assign out_4 = Val_p;
endmodule

// PC increment
module PC_INCREMENT (
  input  [15:0] PC_IN,
  output [15:0] PC_OUTPUT
);

  Adder #(.width(16)) adder_1 (.a(PC_IN), .b(16'h6), .out(PC_OUTPUT));  // open: cin, cout
endmodule

module PC (
  input  input_enabler,
  input  [15:0] Input,
  input  Clear,
  output [15:0] Output
);

  wire clock_1_out, not_1_out;
  wire [15:0] adder_1_out, controlled_buffer_1_out;

  not not_1 (not_1_out, input_enabler);
  assign controlled_buffer_1_out = not_1_out ? adder_1_out : 16'bz;  // Controlled_Buffer controlled_buffer_1
  assign controlled_buffer_1_out = input_enabler ? Input : 16'bz;  // Controlled_Buffer controlled_buffer_2
  Clock clock_1 (.out(clock_1_out));
  Register #(.width(16)) register_1 (
    .D(controlled_buffer_1_out), .Q(Output), .clk(clock_1_out), .clr(Clear));  // open: en
  Adder #(.width(16)) adder_1 (.a(Output), .b(16'h1), .out(adder_1_out));  // open: cin, cout
endmodule

// FETCH UNIT
module Fetch (
  input  [15:0] PC_IN,
  input  Halt,
  output [3:0] Icode,
  output [3:0] ifun,
  output [3:0] RA,
  output [3:0] RB,
  output [31:0] Val_C,
  output enable,
  output [15:0] PC_out
);

  wire buffer_1_out, clock_1_out, d_ff_1_q, demultiplexer_1_out0, demultiplexer_1_out1, demultiplexer_1_out2,
       not_1_out, undriven;
  wire [1:0] bitselector_1_out;
  wire [15:0] adder_1_out, multiplexer_1_out, register_1_q, register_2_q;
  wire [31:0] register_3_q, register_4_q, rom_1_data;

  Clock clock_1 (.out(clock_1_out));
  Register #(.width(16)) register_1 (.Q(register_1_q), .clk(buffer_1_out));  // open: D, en, clr
  Register #(.width(16)) register_2 (.D(PC_IN), .Q(register_2_q), .clk(buffer_1_out));  // open: en, clr
  buf buffer_1 (buffer_1_out, clock_1_out);
  not not_1 (not_1_out, d_ff_1_q);
  D_Flip_Flop d_ff_1 (.clk(d_ff_1_q), .Q(d_ff_1_q), .preset(Halt));  // open: D, Qn, en, reset
  Adder #(.width(16)) adder_1 (.a(register_1_q), .b(register_2_q), .out(adder_1_out));  // open: cin, cout
  BitSelector #(.width(16), .group(2)) bitselector_1 (.in(register_1_q), .out(bitselector_1_out), .sel(3'b000));
  Multiplexer #(.width(16)) multiplexer_1 (
    .in0(adder_1_out), .in1(register_2_q), .out(multiplexer_1_out), .sel(d_ff_1_q));  // open: en
  ROM #(.addrWidth(16), .dataWidth(32)) rom_1 (.addr(multiplexer_1_out), .data(rom_1_data));  // open: sel
  Adder #(.width(16)) adder_2 (.a(16'h6), .b(register_2_q), .out(PC_out));  // open: cin, cout
  Demultiplexer #(.select(2)) demultiplexer_1 (
    .out0(demultiplexer_1_out0), .out1(demultiplexer_1_out1), .out2(demultiplexer_1_out2), .out3(enable),
    .in(1'b1), .sel(bitselector_1_out));  // open: en
  Register #(.width(32)) register_3 (
    .D(rom_1_data), .en(demultiplexer_1_out0), .Q(register_3_q), .clk(undriven));  // open: clr
  BitSelector #(.width(32), .group(4)) bitselector_2 (.in(register_4_q), .out(RA), .sel(3'b011));
  Register #(.width(32)) register_4 (
    .D(rom_1_data), .en(demultiplexer_1_out1), .Q(register_4_q), .clk(undriven));  // open: clr
  BitSelector #(.width(32), .group(4)) bitselector_3 (.in(register_4_q), .out(RB), .sel(3'b100));
  Register #(.width(32)) register_5 (
    .D(rom_1_data), .en(demultiplexer_1_out2), .Q(Val_C), .clk(undriven));  // open: clr
  BitSelector #(.width(32), .group(4)) bitselector_4 (.in(register_3_q), .out(Icode), .sel(3'b000));
  BitSelector #(.width(32), .group(4)) bitselector_5 (.in(register_3_q), .out(ifun), .sel(3'b001));
endmodule

module Register_File (
  input  [31:0] Write1,
  input  RE,
  input  [3:0] Register_1,
  input  [3:0] Register_1_2,
  input  WE,
  input  [3:0] Register_2,
  input  [3:0] Register_2_2,
  input  [31:0] Write2,
  output [31:0] Read1,
  output [31:0] Read2
);

  wire clock_1_out, decoder_1_out0, decoder_1_out1, decoder_1_out2, decoder_1_out3, decoder_1_out4,
       decoder_1_out5, decoder_1_out6, decoder_1_out7, decoder_2_out0, decoder_2_out1, decoder_2_out2,
       decoder_2_out3, decoder_2_out4, decoder_2_out5, decoder_2_out6, decoder_2_out7, decoder_3_out0,
       decoder_3_out1, decoder_3_out2, decoder_3_out3, decoder_3_out4, decoder_3_out5, decoder_3_out6,
       decoder_3_out7, decoder_4_out0, decoder_4_out1, decoder_4_out2, decoder_4_out3, decoder_4_out4,
       decoder_4_out5, decoder_4_out6, decoder_4_out7, or_1_out, or_2_out, or_3_out, or_4_out, or_5_out,
       or_6_out, or_7_out, or_8_out;
  wire [31:0] multiplexer_1_out, multiplexer_2_out, multiplexer_3_out, multiplexer_4_out, multiplexer_5_out,
       multiplexer_6_out, multiplexer_7_out, multiplexer_8_out, register_1_q, register_2_q, register_3_q,
       register_4_q, register_5_q, register_6_q, register_7_q, register_8_q;

  Decoder #(.select(4)) decoder_1 (
    .out0(decoder_1_out0), .out1(decoder_1_out1), .out2(decoder_1_out2), .out3(decoder_1_out3),
    .out4(decoder_1_out4), .out5(decoder_1_out5), .out6(decoder_1_out6), .out7(decoder_1_out7),
    .sel(Register_1_2), .en(WE));  // open: out8, out9, out10, out11, out12, out13, out14, out15
  Decoder #(.select(4)) decoder_2 (
    .out0(decoder_2_out0), .out1(decoder_2_out1), .out2(decoder_2_out2), .out3(decoder_2_out3),
    .out4(decoder_2_out4), .out5(decoder_2_out5), .out6(decoder_2_out6), .out7(decoder_2_out7),
    .sel(Register_2_2), .en(WE));  // open: out8, out9, out10, out11, out12, out13, out14, out15
  Multiplexer #(.width(32)) multiplexer_1 (
    .in0(Write2), .in1(Write1), .out(multiplexer_1_out), .sel(decoder_1_out0));  // open: en
  Multiplexer #(.width(32)) multiplexer_2 (
    .in0(Write2), .in1(Write1), .out(multiplexer_2_out), .sel(decoder_1_out1));  // open: en
  Multiplexer #(.width(32)) multiplexer_3 (
    .in0(Write2), .in1(Write1), .out(multiplexer_3_out), .sel(decoder_1_out2));  // open: en
  Multiplexer #(.width(32)) multiplexer_4 (
    .in0(Write2), .in1(Write1), .out(multiplexer_4_out), .sel(decoder_1_out3));  // open: en
  Multiplexer #(.width(32)) multiplexer_5 (
    .in0(Write2), .in1(Write1), .out(multiplexer_5_out), .sel(decoder_1_out4));  // open: en
  Multiplexer #(.width(32)) multiplexer_6 (
    .in0(Write2), .in1(Write1), .out(multiplexer_6_out), .sel(decoder_1_out5));  // open: en
  Multiplexer #(.width(32)) multiplexer_7 (
    .in0(Write2), .in1(Write1), .out(multiplexer_7_out), .sel(decoder_1_out6));  // open: en
  Multiplexer #(.width(32)) multiplexer_8 (
    .in0(Write2), .in1(Write1), .out(multiplexer_8_out), .sel(decoder_1_out7));  // open: en
  or or_1 (or_1_out, decoder_1_out0, decoder_2_out0);
  or or_2 (or_2_out, decoder_1_out1, decoder_2_out1);
  or or_3 (or_3_out, decoder_1_out2, decoder_2_out2);
  or or_4 (or_4_out, decoder_1_out3, decoder_2_out3);
  or or_5 (or_5_out, decoder_1_out4, decoder_2_out4);
  or or_6 (or_6_out, decoder_1_out5, decoder_2_out5);
  or or_7 (or_7_out, decoder_1_out6, decoder_2_out6);
  or or_8 (or_8_out, decoder_1_out7, decoder_2_out7);
  Clock clock_1 (.out(clock_1_out));
  Register #(.width(32)) u_register_1 (
    .D(multiplexer_1_out), .en(or_1_out), .Q(register_1_q), .clk(clock_1_out));  // open: clr
  Register #(.width(32)) u_register_2 (
    .D(multiplexer_2_out), .en(or_2_out), .Q(register_2_q), .clk(clock_1_out));  // open: clr
  Register #(.width(32)) register_3 (
    .D(multiplexer_3_out), .en(or_3_out), .Q(register_3_q), .clk(clock_1_out));  // open: clr
  Register #(.width(32)) register_4 (
    .D(multiplexer_4_out), .en(or_4_out), .Q(register_4_q), .clk(clock_1_out));  // open: clr
  Register #(.width(32)) register_5 (
    .D(multiplexer_5_out), .en(or_5_out), .Q(register_5_q), .clk(clock_1_out));  // open: clr
  Register #(.width(32)) register_6 (
    .D(multiplexer_6_out), .en(or_6_out), .Q(register_6_q), .clk(clock_1_out));  // open: clr
  Register #(.width(32)) register_7 (
    .D(multiplexer_7_out), .en(or_7_out), .Q(register_7_q), .clk(clock_1_out));  // open: clr
  Register #(.width(32)) register_8 (
    .D(multiplexer_8_out), .en(or_8_out), .Q(register_8_q), .clk(clock_1_out));  // open: clr
  assign Read1 = decoder_3_out0 ? register_1_q : 32'bz;  // Controlled_Buffer controlled_buffer_1
  assign Read1 = decoder_3_out1 ? register_2_q : 32'bz;  // Controlled_Buffer controlled_buffer_2
  assign Read1 = decoder_3_out2 ? register_3_q : 32'bz;  // Controlled_Buffer controlled_buffer_3
  assign Read1 = decoder_3_out3 ? register_4_q : 32'bz;  // Controlled_Buffer controlled_buffer_4
  assign Read1 = decoder_3_out4 ? register_5_q : 32'bz;  // Controlled_Buffer controlled_buffer_5
  assign Read1 = decoder_3_out5 ? register_6_q : 32'bz;  // Controlled_Buffer controlled_buffer_6
  assign Read1 = decoder_3_out6 ? register_7_q : 32'bz;  // Controlled_Buffer controlled_buffer_7
  assign Read1 = decoder_3_out7 ? register_8_q : 32'bz;  // Controlled_Buffer controlled_buffer_8
  assign Read2 = decoder_4_out0 ? register_1_q : 32'bz;  // Controlled_Buffer controlled_buffer_9
  assign Read2 = decoder_4_out1 ? register_2_q : 32'bz;  // Controlled_Buffer controlled_buffer_10
  assign Read2 = decoder_4_out2 ? register_3_q : 32'bz;  // Controlled_Buffer controlled_buffer_11
  assign Read2 = decoder_4_out3 ? register_4_q : 32'bz;  // Controlled_Buffer controlled_buffer_12
  assign Read2 = decoder_4_out4 ? register_5_q : 32'bz;  // Controlled_Buffer controlled_buffer_13
  assign Read2 = decoder_4_out5 ? register_6_q : 32'bz;  // Controlled_Buffer controlled_buffer_14
  assign Read2 = decoder_4_out6 ? register_7_q : 32'bz;  // Controlled_Buffer controlled_buffer_15
  assign Read2 = decoder_4_out7 ? register_8_q : 32'bz;  // Controlled_Buffer controlled_buffer_16
  Decoder #(.select(4)) decoder_3 (
    .out0(decoder_3_out0), .out1(decoder_3_out1), .out2(decoder_3_out2), .out3(decoder_3_out3),
    .out4(decoder_3_out4), .out5(decoder_3_out5), .out6(decoder_3_out6), .out7(decoder_3_out7),
    .sel(Register_1), .en(RE));  // open: out8, out9, out10, out11, out12, out13, out14, out15
  Decoder #(.select(4)) decoder_4 (
    .out0(decoder_4_out0), .out1(decoder_4_out1), .out2(decoder_4_out2), .out3(decoder_4_out3),
    .out4(decoder_4_out4), .out5(decoder_4_out5), .out6(decoder_4_out6), .out7(decoder_4_out7),
    .sel(Register_2), .en(RE));  // open: out8, out9, out10, out11, out12, out13, out14, out15
endmodule

module ALU (
  input  [7:0] A,
  input  [7:0] B,
  input  in_3,
  input  [3:0] Instruction,
  output [7:0] Output,
  output GE,
  output GZ,
  output LZ,
  output LE,
  output EQ
);

  wire clock_1_out, comparator_1_eq, comparator_1_gt, comparator_1_lt, or_1_out, or_2_out;
  wire [7:0] adder_1_out, multiplier_1_out, subtractor_1_out;

  Comparator comparator_1 (.a(A), .b({8{1'b0}}), .gt(comparator_1_gt), .eq(comparator_1_eq), .lt(comparator_1_lt));
  or or_1 (or_1_out, comparator_1_lt, comparator_1_eq);
  Register #(.width(1)) register_1 (.D(comparator_1_lt), .Q(LZ), .clk(clock_1_out));  // open: en, clr
  Adder adder_1 (.a(A), .b(B), .out(adder_1_out));  // open: cin, cout
  Subtractor subtractor_1 (.a(A), .b(B), .out(subtractor_1_out));  // open: bin, bout
  Multiplier multiplier_1 (.a(A), .b(B), .out(multiplier_1_out));  // open: cin, cout
  Register #(.width(1)) register_2 (.D(or_1_out), .Q(LE), .clk(clock_1_out));  // open: en, clr
  or or_2 (or_2_out, comparator_1_eq, comparator_1_gt);
  Register #(.width(1)) register_3 (.D(comparator_1_eq), .Q(EQ), .clk(clock_1_out));  // open: en, clr
  Register #(.width(1)) register_4 (.D(or_2_out), .Q(GE), .clk(clock_1_out));  // open: en, clr
  Register #(.width(1)) register_5 (.D(comparator_1_gt), .Q(GZ), .clk(clock_1_out));  // open: en, clr
  Multiplexer #(.select(4), .width(8)) multiplexer_1 (
    .in0({8{1'b0}}), .in1({8{1'b0}}), .in2({8{1'b0}}), .in3({8{1'b0}}), .in4(adder_1_out),
    .in5(subtractor_1_out), .in6({8{1'b0}}), .in7(multiplier_1_out), .in8({8{1'b0}}), .in9({8{1'b0}}),
    .in10({8{1'b0}}), .in11({8{1'b0}}), .in12({8{1'b0}}), .in13({8{1'b0}}), .in14({8{1'b0}}),
    .in15({8{1'b0}}), .out(Output), .sel(Instruction), .en(in_3));
  Clock clock_1 (.out(clock_1_out));
endmodule
